# Fritzing sketch Circuito bluetooth led fritzing (saved by Fritzing 0.9.3b)
breadboards: 1

parts:
  Componente1 = Bluetooth HC-05
  Componente2 = Arduino Uno (Rev3)
  LED1 = LED - 5mm [color="Red (633nm)" package="5 mm [THT]"]
  R1 = Resistor [tolerance=±5% resistance=220 package=THT]

nets:
  N1: Componente1.RXD, Componente2.D1/TX
  N2: Componente1.TXD, Componente2.D0/RX
  GND: Componente1.GND, Componente2.GND, LED1.anode
  VCC: Componente1.VCC, Componente2.5V
  N3: Componente2.D13/SCK, R1.Pin_0
  N4: LED1.cathode, R1.Pin_1
