# Fritzing sketch Untitled Sketch (saved by Fritzing 0.9.3b)
breadboards: 1

parts:
  M1 = DC Motor
  Bluetooth = Bluetooth HC-06
  Q1 = NPN-Transistor [package="TO92 [THT]"]
  Componente2 = Arduino Uno (Rev3)
  R1 = Resistor [tolerance=±5% resistance=220 package=THT]
  VCC1 = Battery

nets:
  N1: M1.pin_1, VCC1.+
  N2: M1.pin_2, Q1.B
  N3: Bluetooth.RXD, Componente2.D1/TX
  N4: Bluetooth.TXD, Componente2.D0/RX
  GND: Bluetooth.GND, Q1.E, Componente2.GND, VCC1.-
  N5: Bluetooth.VCC, Componente2.D2
  N6: Q1.C, R1.Pin_0
  N7: Componente2.D9_PWM, R1.Pin_1
