# Fritzing sketch Untitled Sketch (saved by Fritzing 0.9.3b)
breadboards: 1

parts:
  SIM800L_BO1 = SIM800L BO
  Componente1 = Arduino Uno (Rev3)
  BAT1 = Battery Holders [package=lipo-1100mAh]
  S1 = Pushbutton [package="[THT]"]
  R1 = Resistor [tolerance=±5% resistance=10k package=THT]
  LED1 = LED - 5mm [color="Red (633nm)" package="5 mm [THT]"]

nets:
  N1: SIM800L_BO1.PIN2, BAT1.+
  N2: SIM800L_BO1.pin_4, Componente1.D9_PWM
  N3: SIM800L_BO1.pin_5, Componente1.D8
  N4: SIM800L_BO1.pin_6, Componente1.GND, BAT1.-, R1.Pin_1, LED1.cathode
  N5: Componente1.D13/SCK, LED1.anode
  N6: Componente1.D3_PWM, S1.Pin_1, S1.Pin_2, R1.Pin_0
  N7: Componente1.5V, S1.Pin_3, S1.Pin_4
