# Fritzing sketch Motor velocidad  variab pot (saved by Fritzing 0.9.3b)
breadboards: 1

parts:
  M1 = DC Motor
  U1 = TRANSISTOR_NPN_2 [package=to-92]
  Componente1 = Arduino Uno (Rev3)
  R1 = Resistor [tolerance=±5% resistance=1k package=THT]
  R2 = Rotary Potentiometer (Small) [maximum_resistance=10kΩ package=THT]
  VCC1 = Battery block 9V
  D1 = Rectifier Diode [part_number=1N4001 package="300 mil [THT]"]

nets:
  N1: M1.pin_1, Componente1.GND, VCC1.+, D1.cathode
  N2: M1.pin_2, U1.B, D1.anode
  N3: U1.C, R2.leg2, VCC1.-
  N4: U1.E, R1.Pin_0
  N5: Componente1.A0, R2.wiper
  N6: Componente1.D12/MISO, R1.Pin_1
  N7: Componente1.5V, R2.leg1
