# Fritzing sketch Motor pulsador (saved by Fritzing 0.9.3b)
breadboards: 1

parts:
  Pulsador = Pushbutton [package="[THT]"]
  M1 = DC Motor
  Componente1 = Arduino Uno (Rev3)
  BD139 = NPN-Transistor [package="TO92 [THT]"]
  R1 = Resistor [tolerance=±20% resistance=10k package=THT]
  R2 = Resistor [tolerance=±5% resistance=1k package=THT]
  BAT1 = BC9VPC [package=bc9vpc]
  Diodo = Rectifier Diode [part_number=1N4001 package="300 mil [THT]"]

nets:
  N1: Pulsador.Pin_1, Pulsador.Pin_2, Componente1.D7, R1.Pin_0
  N2: Pulsador.Pin_3, Pulsador.Pin_4, Componente1.5V
  N3: M1.pin_1, BAT1.V+, Diodo.cathode
  N4: M1.pin_2, BD139.B, Diodo.anode
  N5: Componente1.D10_PWM/SS, R2.Pin_1
  N6: Componente1.GND, BD139.E, R1.Pin_1, BAT1.V-
  N7: BD139.C, R2.Pin_0
