# Fritzing sketch Circuito 1 motor puente h (saved by Fritzing 0.9.3b)
breadboards: 1

parts:
  VCC1 = Battery
  M2 = DC Motor
  Arduino_uno = Arduino Uno (Rev3)
  IC3 = L293D [package=THT]

nets:
  GND: VCC1.-, Arduino_uno.GND, IC3.0V
  N1: VCC1.+, IC3.+Vmotor
  N2: M2.pin_1, IC3.Out_4_(_Controlled_by_Enable_2_)
  N3: M2.pin_2, IC3.Out_3_(_Controlled_by_Enable_2_)
  N4: Arduino_uno.D9_PWM, IC3.In_3
  N5: Arduino_uno.D10_PWM/SS, IC3.In_4
  N6: Arduino_uno.5V, IC3.+V
