# Fritzing sketch Circuito en protoboard (saved by Fritzing 1.0.4)
breadboards: 1

parts:
  Componente2 = Jtron 1 Channel Optoisolated Relay Module [package=relay]
  YwRobot_Power_Supply1 = YwRobot Breadboard Power Supply [part_number=545043]
  LED1 = LED - 5mm [color="Red (633nm)" current=0.030A package="5 mm [THT]"]
  Componente3 = Arduino Uno (Rev3)
  R1 = Resistor [tolerance=±5% resistance=220 package="0805 [SMD]"]

nets:
  N1: Componente2.VCC, Componente3.D12/MISO
  N2: Componente2.NO, R1.Pin_1
  N3: Componente2.MAIN, YwRobot_Power_Supply1.VCC#9
  N4: Componente2.IN1, YwRobot_Power_Supply1.VCC#5
  GND: Componente2.GND, YwRobot_Power_Supply1.GND#11, Componente3.GND
  N5: YwRobot_Power_Supply1.GND#13, LED1.cathode
  N6: LED1.anode, R1.Pin_0

custom parts:
  YwRobot Breadboard Power Supply: The YwRobot Breadboard Power Supply (MB-V2) has two power rails; they can be 5V or 3V3. Power to the module can be provided through the female USB socket or through the A10 (female) 2.1mm power jack.
