# Fritzing sketch ReléActivDesactivMotDC (saved by Fritzing 1.0.4)
breadboards: 1

parts:
  YwRobot_Power_Supply1 = YwRobot Breadboard Power Supply [part_number=545043]
  M1 = DC Motor [voltage_(max)=6V voltage_(min)=3V]
  Componente1 = Jtron 1 Channel Optoisolated Relay Module [package=relay]
  Componente2 = Arduino Uno (Rev3)

nets:
  N1: YwRobot_Power_Supply1.VCC#5, YwRobot_Power_Supply1.VCC#6, Componente1.IN1
  N2: YwRobot_Power_Supply1.VCC#9, YwRobot_Power_Supply1.VCC#10, Componente1.NO
  N3: YwRobot_Power_Supply1.GND#11, YwRobot_Power_Supply1.GND#12, Componente2.GND
  N4: YwRobot_Power_Supply1.GND#13, YwRobot_Power_Supply1.GND#14, M1.pin_1, Componente1.GND
  N5: M1.pin_2, Componente1.MAIN
  N6: Componente1.VCC, Componente2.D12/MISO

custom parts:
  YwRobot Breadboard Power Supply: The YwRobot Breadboard Power Supply (MB-V2) has two power rails; they can be 5V or 3V3. Power to the module can be provided through the female USB socket or through the A10 (female) 2.1mm power jack.
