# Fritzing sketch Circuito sensor magnetico (saved by Fritzing 0.9.3b)
breadboards: 1

parts:
  Componente1 = Arduino Uno (Rev3)
  S1 = Reed switch [package=THT]
  10_K = Resistor [tolerance=±5% resistance=220 package=THT]
  J1 = Piezo Speaker

nets:
  N1: Componente1.D9_PWM, J1.pin2
  N2: Componente1.D7, S1.pin_2, 10_K.Pin_1
  N3: Componente1.5V, 10_K.Pin_0
  N4: Componente1.GND, S1.pin_1, J1.pin1
