# Fritzing sketch Sensor Tem-Hum DHT (saved by Fritzing 0.9.3b)
circuit board: 8.46667cm x 5.64444cm
breadboards: 1

parts:
  RHT1 = Humidity and Temperature Sensor RHT03
  Componente1 = Arduino Uno (Rev3) - ICSP
  R1 = Resistor [tolerance=±5% resistance=4.7k package=THT]

nets:
  VCC: RHT1.Vcc, Componente1.5V, R1.Pin_0
  N1: RHT1.Data-signal, Componente1.D10_PWM/SS, R1.Pin_1
  N2: RHT1.GND_2, Componente1.GND

notes:
  HDT22
  R=4,7 Kohm

// code stored in the sketch: ser.ino
#include <DHT.h>


DHT dht(10, DHT11); // O DHT22 según el sensor que usemos.


void setup()
{
  Serial.begin(9600); 
  Serial.println("Prueba DHT11:");
  dht.begin();
}


void loop()
{
  // Se lee la humedad y la temperatura del sensor:
  float h = dht.readHumidity();
  float t = dht.readTemperature();


  // Si los valores leídos no son números se advierte de ello, de lo contrario se imprimen los resultados:
  if(isnan(t) || isnan(h))
  {
    Serial.println("Fallo de lectura del DHT");
  }
  else
  {
    Serial.print("Humedad: ");     Serial.print(h); Serial.print(" %\t");
    Serial.print("Temperatura: "); Serial.print(t); Serial.print(" *C\n");
  }
  delay(1000);
}
