# Fritzing sketch Sens ultra (saved by Fritzing 0.9.3b)

parts:
  Componente1 = Arduino Uno (Rev3)
  hc-sr1 = hc-sr04

nets:
  N1: Componente1.D8, hc-sr1.Echo
  N2: Componente1.D9_PWM, hc-sr1.Trig
  5V: Componente1.5V, hc-sr1.VCC
  GND: Componente1.GND, hc-sr1.GND
