# Fritzing sketch Circuito Arduino-Cmp (saved by Fritzing 0.9.3b)
breadboards: 1

parts:
  Transistor_TIP_122 = npn-Powertransistor [package="TO220 [THT]"]
  RHT1 = Humidity and Temperature Sensor RHT03
  R1 = Resistor [tolerance=±5% resistance=10k package=THT]
  Componente1 = Arduino Uno (Rev3)
  BAT1 = BC9VPC [package=bc9vpc]
  LED1 = LED - 5mm [color="Red (633nm)" package="5 mm [THT]"]
  Motor_DC = DC Motor
  R2 = Resistor [tolerance=±20% resistance=1k package="1206 [SMD]"]

nets:
  N1: Transistor_TIP_122.base, R2.Pin_1
  N2: Transistor_TIP_122.collector, Motor_DC.pin_2
  N3: Transistor_TIP_122.emitter, RHT1.GND_2, Componente1.GND, BAT1.V-, LED1.anode
  VCC: RHT1.Vcc, R1.Pin_1, Componente1.5V
  N4: RHT1.Data-signal, R1.Pin_0, Componente1.D2
  N5: Componente1.D13/SCK, LED1.cathode
  N6: Componente1.D3_PWM, R2.Pin_0
  N7: BAT1.V+, Motor_DC.pin_1
